# Fritzing sketch Arduino 2 -1 (saved by Fritzing 1.0.3b)
breadboards: 1

parts:
  Part1 = Arduino Uno (Rev3) - ICSP
  R1 = TRIMPOT [maximum_resistance=10kΩ knob_status=50% power=0.5W package=trimpot_pth_s3_lock]

nets:
  N1: Part1.A0, R1.WIPER
  N2: Part1.5V, R1.CCW
  N3: Part1.GND, R1.CW
